# Fritzing sketch arduino-pi-sp (saved by Fritzing 0.9.3b)

parts:
  Raspberry_Pi_1 = Raspberry Pi 3 [part_number=RPI-3-V1.2]
  Adafruit_Circuit_Playground_Express = Adafruit Circuit Playground Express [part_number=ATSAMD21]

nets:
  GND: Raspberry_Pi_1.GPIO3, Raspberry_Pi_1.GND, Adafruit_Circuit_Playground_Express.GND
  N1: Raspberry_Pi_1.GPIO15, Adafruit_Circuit_Playground_Express.D1_A7_TX
  N2: Raspberry_Pi_1.GPIO14, Adafruit_Circuit_Playground_Express.D0_A6_RX

custom parts:
  Adafruit Circuit Playground Express: Circuit Playground Express is the next step towards a perfect introduction to electronics and programming. We've taken the original Circuit Playground Classic and made it even better! Not only did we pack even more sensors in, we also made it even easier to program. You can now start your journey with Microsoft MakeCode block-based or Javascript programming. Then, you can use the same board to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
