# Fritzing sketch rpi-led (saved by Fritzing 0.9.6b)
breadboards: 1

parts:
  Raspberry_Pi_1 = Raspberry Pi 3 [part_number=RPI-3-V1.2]
  LED1 = LED - 5mm [color="Red (633nm)" current=0.030 package="5 mm [THT]"]
  R1 = Resistor [tolerance=±5% resistance=220 power=0.25 package=THT]

nets:
  N1: Raspberry_Pi_1.GPIO18, LED1.anode
  N2: Raspberry_Pi_1.GND, R1.Pin_1
  N3: LED1.cathode, R1.Pin_0
