# Fritzing sketch rpi-more-blinking-lights (saved by Fritzing 0.9.6b)
breadboards: 1

parts:
  Raspberry_Pi_1 = Raspberry Pi 3 [part_number=RPI-3-V1.2]
  POT1 = Breadboard Trimpot
  IC1 = MCP3008 8-channel 10-bit ADC [part_number=MCP3008]
  LED1 = LED - 5mm [color="Red (633nm)" current=0.030 package="5 mm [THT]"]
  R1 = Resistor [tolerance=±5% resistance=220 power=0.25 package=THT]
  R2 = Resistor [tolerance=±5% resistance=220 power=0.25 package=THT]
  LED2 = LED - 5mm [color="Red (633nm)" current=0.030 package="5 mm [THT]"]
  LED3 = LED - 5mm [color="Red (633nm)" current=0.030 package="5 mm [THT]"]
  R3 = Resistor [tolerance=±5% resistance=220 power=0.25 package=THT]
  S1 = Pushbutton [package="[THT]"]

nets:
  N1: Raspberry_Pi_1.3v3, POT1.PIN3, IC1.no_name_yet#15, IC1.no_name_yet#16, S1.Pin_3, S1.Pin_4
  N2: Raspberry_Pi_1.GPIO10, IC1.no_name_yet#13
  N3: Raspberry_Pi_1.GPIO9, IC1.no_name_yet#12
  N4: Raspberry_Pi_1.GPIO11, IC1.no_name_yet#11
  N5: Raspberry_Pi_1.GPIO21, R3.Pin_1
  N6: Raspberry_Pi_1.GPIO20, R2.Pin_1
  N7: Raspberry_Pi_1.GPIO16, R1.Pin_1
  N8: Raspberry_Pi_1.GPIO12, S1.Pin_1, S1.Pin_2
  N9: Raspberry_Pi_1.GPIO8, IC1.no_name_yet#10
  N10: Raspberry_Pi_1.GND, POT1.PIN1, IC1.no_name_yet#9, IC1.no_name_yet#14, LED1.cathode, LED2.cathode, LED3.cathode
  N11: POT1.PIN2, IC1.no_name_yet#1
  N12: LED1.anode, R1.Pin_0
  N13: R2.Pin_0, LED2.anode
  N14: LED3.anode, R3.Pin_0
