# Fritzing sketch ci-setup (saved by Fritzing 0.9.3b)
breadboards: 1

parts:
  Raspberry_Pi_1 = Raspberry Pi 3 [part_number=RPI-3-V1.2]
  ADC1 = MCP3008 [package=dil16]
  Part1 = BME280 Breakout
  R1 = Resistor [tolerance=±5% resistance=4.7k package=THT]
  C1 = Capacitor [package=cap-pth-small2]
  R2 = Resistor [tolerance=±5% resistance=10k package=THT]
  R3 = Resistor [tolerance=±5% resistance=4.7k package=THT]
  R4 = Resistor [tolerance=±5% resistance=4.7k package=THT]

nets:
  3V3: Raspberry_Pi_1.3v3, ADC1.CH7, ADC1.VREF, ADC1.VDD, Part1.3.3V, R4.Pin_0
  N1: Raspberry_Pi_1.GPIO2, Part1.SDI/SDA
  N2: Raspberry_Pi_1.GPIO3, Part1.!CS
  N3: Raspberry_Pi_1.GPIO10, ADC1.Din
  N4: Raspberry_Pi_1.GPIO9, ADC1.Dout
  N5: Raspberry_Pi_1.GPIO11, ADC1.CLK
  N6: Raspberry_Pi_1.GPIO5, R2.Pin_0
  N7: Raspberry_Pi_1.GPIO6, R2.Pin_1
  N8: Raspberry_Pi_1.GPIO8, ADC1.CS/SHDN
  N9: Raspberry_Pi_1.GPIO18, R1.Pin_1
  GND: Raspberry_Pi_1.GND, ADC1.CH6, ADC1.DGND, ADC1.AGND, Part1.GND, C1.2, R3.Pin_1
  N10: ADC1.CH0, R1.Pin_0, C1.1
  N11: ADC1.CH5, R3.Pin_0, R4.Pin_1

notes:
  BME280 in the lab doesn't look like the one on the picture. It is connected directly to breadboard and layout on the breadboard represents actual pins
  SPI0
  I2C1
  SPI0 from left to right
  MOSI; MISO; SCLK; CE0
  I2C1 from left to right
  SDA; SCL
  PWM0
  Low pass filter params:
  R=4.7k ohm
  C=0.1 uF
  V=3.3V
  f_PWM=10kHz
  settling time: ~1.1ms
  peak to peak: 0.18V [~5.5%]
  TODO
  Add 74LS157 (2:1 mux)
  to swap between BME280's SPI/I2C
  since they share pins
  R1 = 10k ohm
  R1
  2x 4.7k ohm
  0.5VCC
