# Fritzing sketch ADS1115_circuit (saved by Fritzing 0.9.3b)

parts:
  元件1 = ADS1115
  Raspberry_Pi_1 = Raspberry Pi 3 [part_number=RPI-3-V1.2]
  R1 = Rotary Potentiometer (Small) [maximum_resistance=100kΩ package=THT]

nets:
  VDD: 元件1.VDD, Raspberry_Pi_1.5V, R1.leg1
  GND: 元件1.GND, 元件1.ADDR, Raspberry_Pi_1.GND, R1.leg2
  N1: 元件1.SCL, Raspberry_Pi_1.GPIO3
  N2: 元件1.SDA, Raspberry_Pi_1.GPIO2
  N3: 元件1.A0, R1.wiper

custom parts:
  ADS1115: ADC ADS1115
