# Fritzing sketch ADXL345_circuit (saved by Fritzing 0.9.3b)

parts:
  元件1 = Triple Axis Accelerometer Breakout - ADXL345
  Raspberry_Pi_1 = Raspberry Pi 3 [part_number=RPI-3-V1.2]

nets:
  GND: 元件1.GND, Raspberry_Pi_1.GND
  VCC: 元件1.VCC, Raspberry_Pi_1.3v3
  N1: 元件1.CS, Raspberry_Pi_1.GPIO8
  N2: 元件1.SDO, Raspberry_Pi_1.GPIO9
  N3: 元件1.SDA, Raspberry_Pi_1.GPIO10
  N4: 元件1.SCL, Raspberry_Pi_1.GPIO11
