# Fritzing sketch AGS01DB_circuit (saved by Fritzing 0.9.3b)
breadboards: 1

parts:
  Raspberry_Pi_1 = Raspberry Pi 3 [part_number=RPI-3-V1.2]
  DHT3 = DHT11 Humitidy and Temperature Sensor
  R1 = Resistor [tolerance=±5% resistance=4.7k package=THT]
  R2 = Resistor [tolerance=±5% resistance=4.7k package=THT]

nets:
  N1: Raspberry_Pi_1.GPIO2, DHT3.DATA, R1.Pin_0
  N2: Raspberry_Pi_1.GPIO3, DHT3.GND, R2.Pin_0
  N3: Raspberry_Pi_1.GND, DHT3.NULL
  5V: Raspberry_Pi_1.5V, DHT3.VDD, R1.Pin_1, R2.Pin_1

notes:
  AGS01DB

custom parts:
  DHT11 Humitidy and Temperature Sensor: DHT11 Humidity and Temperature Sensor
