# Fritzing sketch ArduinoSample (saved by Fritzing 0.9.5d)
breadboards: 2

parts:
  S1 = Pushbutton [package="[THT]"]
  R1 = Resistor [tolerance=±5% resistance=10k package=THT]
  LED2 = LED - 5mm [color="Yellow (592nm)" package="5 mm [THT]"]
  LED3 = LED - 5mm [color="Red (633nm)" package="5 mm [THT]"]
  Part1 = Arduino Nano (Rev3.0)
  LED1 = LED - 5mm [color="Green (565nm)" package="5 mm [THT]"]
  BMP280 = Barometric Pressure Sensor - BMP180 Breakout (GY-68)
  LCD1 = LCD screen
  R2 = Resistor [tolerance=±5% resistance=560 package=THT]
  R3 = Trimmer Potentiometer [maximum_resistance=10kΩ package=THT]
  M1 = Humidity and Temperature Sensor DHT11

nets:
  VCC: S1.Pin_1, S1.Pin_2, Part1.5V, BMP280.VCC, LCD1.VDD, R2.Pin_0, R3.leg1, M1.Vcc
  N1: S1.Pin_3, S1.Pin_4, R1.Pin_1, Part1.D2
  GND: R1.Pin_0, LED2.anode, LED3.anode, Part1.GND, LED1.anode, BMP280.GND, LCD1.VSS, LCD1.R/W, LCD1.LED-, R3.leg2, M1.GND
  N2: LED2.cathode, Part1.D8, LCD1.RS
  N3: LED3.cathode, Part1.D6, LCD1.DB6
  N4: Part1.D3, M1.Data
  N5: Part1.D4, LCD1.DB4
  N6: Part1.D5, LCD1.DB5
  N7: Part1.D7, LCD1.DB7
  N8: Part1.D9, LCD1.E
  N9: Part1.D10, LED1.cathode
  N10: Part1.A5, BMP280.SCL
  N11: Part1.A4, BMP280.SDA
  N12: Part1.A1, LCD1.V0, R3.wiper
  N13: LCD1.LED+, R2.Pin_1

notes:
  Note: LEDs with built-in resistors used!

custom parts:
  Humidity and Temperature Sensor DHT11: Digital relative humidity & temperature sensor DHT11
