# Fritzing sketch BH1750FVI_Circuit (saved by Fritzing 0.9.3b)

parts:
  Raspberry_Pi_1 = Raspberry Pi 3 [part_number=RPI-3-V1.2]
  Часть2 = BH1750

nets:
  N1: Raspberry_Pi_1.GPIO2, Часть2.SDA
  N2: Raspberry_Pi_1.GPIO3, Часть2.SCL
  GND: Raspberry_Pi_1.GND, Часть2.GND, Часть2.ADDR
  5V: Raspberry_Pi_1.5V, Часть2.VCC

custom parts:
  BH1750: Light Sensor
