# Fritzing sketch rpi-bmp180_i2c (saved by Fritzing 0.9.3b)
breadboards: 1

parts:
  Raspberry_Pi_1 = Raspberry Pi 3 [part_number=RPI-3-V1.2]
  Componente1 = Barometric Pressure Sensor - BMP180 Breakout (GY-68)

nets:
  3V3: Raspberry_Pi_1.3v3, Componente1.VCC
  N1: Raspberry_Pi_1.GPIO2, Componente1.SDA
  N2: Raspberry_Pi_1.GPIO3, Componente1.SCL
  GND: Raspberry_Pi_1.GND, Componente1.GND
