# Fritzing sketch Buzzer.Samples.wiring (saved by Fritzing 0.9.3b)

parts:
  Raspberry_Pi_1 = Raspberry Pi 3 [part_number=RPI-3-V1.2]
  J1 = Piezo Speaker
  Grove1 = Grove Buzz

nets:
  N1: Raspberry_Pi_1.GPIO26, Grove1.SIG
  GND: Raspberry_Pi_1.GND, J1.pin1, Grove1.GND
  N2: Raspberry_Pi_1.GPIO21, J1.pin2
  5V: Raspberry_Pi_1.5V, Grove1.VCC
