# Fritzing sketch ccs811 (saved by Fritzing 0.9.3b)

parts:
  Raspberry_Pi_1 = Raspberry Pi 3 [part_number=RPI-3-V1.2]
  Composant1 = Adafruit CCS811

nets:
  3V3: Raspberry_Pi_1.3v3, Composant1.VIN
  N1: Raspberry_Pi_1.GIPO17, Composant1.SDA
  N2: Raspberry_Pi_1.GIPO27, Composant1.SCL
  N3: Raspberry_Pi_1.GIPO22, Composant1.!INT
  N4: Raspberry_Pi_1.GIPO23, Composant1.!WAKE
  GND: Raspberry_Pi_1.GND, Composant1.GND
