# Fritzing sketch dcmotor (saved by Fritzing 0.9.3b)
breadboards: 1

parts:
  S1 = H-Bridge with L298N
  Raspberry_Pi_1 = Raspberry Pi 3 [part_number=RPI-3-V1.2]
  M1 = DC Motor
  M2 = DC Motor
  VCC1 = Battery block 9V

nets:
  N1: S1.12V, VCC1.+
  GND: S1.GND, Raspberry_Pi_1.GND, VCC1.-
  5V: S1.5V, Raspberry_Pi_1.5V
  N2: S1.ENA, Raspberry_Pi_1.GIPO23
  N3: S1.IN1, Raspberry_Pi_1.GIPO24
  N4: S1.IN2, Raspberry_Pi_1.GIPO25
  N5: S1.IN3, Raspberry_Pi_1.GIPO5
  N6: S1.IN4, Raspberry_Pi_1.GIPO6
  N7: S1.ENB, S1.ENB-5V
  N8: S1.M1-01, M2.pin_2
  N9: S1.M1-02, M2.pin_1
  N10: S1.M2-01, M1.pin_2
  N11: S1.M2-02, M1.pin_1

notes:
  2 pin setup
  3 pin setup

custom parts:
  H-Bridge with L298N: h-bridge
