# Fritzing sketch DCMotor2pinWithBiDirectionalPin (saved by Fritzing 0.9.3b)

parts:
  Raspberry_Pi_1 = Raspberry Pi 3 [part_number=RPI-3-V1.2]
  Part1 = MD13S
  M1 = DC Motor
  BAT1 = 12 battery [package=battery]

nets:
  N1: Raspberry_Pi_1.GIPO19, Part1.no_name_yet#connector_PWM1
  N2: Raspberry_Pi_1.GIPO26, Part1.no_name_yet#connector_DIR1
  N3: Raspberry_Pi_1.GND, Part1.no_name_yet#connector_G0
  N4: Part1.no_name_yet#connector_MA1, M1.pin_2
  N5: Part1.no_name_yet#connector_MB1, M1.pin_1
  N6: Part1.no_name_yet#connector_N1, BAT1.+
  N7: Part1.no_name_yet#connector_P1, BAT1.-

custom parts:
  12 battery: 12V lead acid type battery, like the Husqvarna YTH2448 12V 35AH battery. This is the mini version 1/4 the size of the actual battery to be closer to typical breadboard parts (around 2in wide rathher than 7in). The pads in pcb are sized to accomidate up to 14ga wire (as these batterys will deliver high currents.)
