# Fritzing sketch DS3231_circuit (saved by Fritzing 0.9.3b)

parts:
  RTC1 = DS3231 AT24C32 Real Time Clock
  Raspberry_Pi_1 = Raspberry Pi 3 [part_number=RPI-3-V1.2]

nets:
  N1: RTC1.SCL, Raspberry_Pi_1.GPIO3
  N2: RTC1.SDA, Raspberry_Pi_1.GPIO2
  VCC: RTC1.VCC, Raspberry_Pi_1.5V
  GND: RTC1.GND, Raspberry_Pi_1.GND

custom parts:
  DS3231 AT24C32 Real Time Clock: Real-time clock basedo on chip DS3231, plus memory chip AT24C32 (32 Kb storage capacity). On-chip temperature sensor with an accuracy of ±3 ℃, I2C bus interface maximum speed: 400 kHz. Operating voltage: 3.3 V to 5.5 V with battery backup capabilities.
