# Fritzing sketch opi_circuit (saved by Fritzing 0.9.5d)
breadboards: 1

parts:
  Orange_Pi_One1 = Orange Pi One [part_number=OPI-ONE]
  S1 = Momentary Switch [package=ksa_sealed_tac_switch]

nets:
  N1: Orange_Pi_One1.PA6, S1.1
  N2: Orange_Pi_One1.GND, S1.3

custom parts:
  Orange Pi One: It’s an open-source single-board computer. It can run Android 4.4, Ubuntu, Debian, Rasberry Pi Image, as well as the banana pi Image. It uses the AllWinner H3 SoC, and has 512MB DDR3 SDRAM
