# Fritzing sketch circuit (saved by Fritzing 0.9.3b)
breadboards: 1

parts:
  part = HC-SR501 Body Sensor Module
  Raspberry_Pi_1 = Raspberry Pi 3 [part_number=RPI-3-V1.2]
  LED1 = LED - 5mm [color="Red (633nm)" package="5 mm [THT]"]
  R1 = Resistor [tolerance=±5% resistance=220 package=THT]

nets:
  VCC: part.VCC, Raspberry_Pi_1.5V
  N1: part.OUT, Raspberry_Pi_1.GIPO17
  GND: part.GND, Raspberry_Pi_1.GND, LED1.cathode
  N2: Raspberry_Pi_1.GIPO27, R1.Pin_1
  N3: LED1.anode, R1.Pin_0

custom parts:
  HC-SR501 Body Sensor Module: Pyroelectric Infrared PIR Motion Sensor Detector Module
