# Fritzing sketch Ina219.Sample (saved by Fritzing 0.9.3b)
breadboards: 1

parts:
  LED3 = LED - 5mm [color="Red (633nm)" package="5 mm [THT]"]
  R3 = Resistor [tolerance=±5% resistance=150 package=THT]
  Part1 = Adafruit T-Cobbler Plus [part_number="Adafruit #1989 and #2028"]
  Part2 = INA219 High Side DC Current Sensor Breakout [part_number=904]

nets:
  GND: LED3.cathode, Part1.GND, Part2.GND
  N1: LED3.anode, R3.Pin_1
  N2: R3.Pin_0, Part2.VIN-
  N3: Part1.SDA, Part2.SDA
  N4: Part1.SCL, Part2.SCL
  N5: Part1.+3.3V_2, Part2.VCC, Part2.VIN+

custom parts:
  Adafruit T-Cobbler Plus: The Raspberry Pi has landed on the Maker World like a 40-GPIO pinned, quad-USB ported, credit card sized bomb of DIY joy. And while you can use most of our great Model B accessories by hooking up our downgrade cable, its probably a good time to upgrade your set up and accessorize using all of the 40 pins. That's why we now carry the Assembled Adafruit Pi T-Cobbler Plus - Breakout + Cable for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
  INA219 High Side DC Current Sensor Breakout: This breakout board will solve all your power-monitoring problems. Instead of struggling with two multimeters, you can just use the handy INA219B chip on this breakout to both measure both the high side voltage and DC current draw over I2C with 1% precision. Most current-measuring devices such as our current panel meter are only good for low side measuring. That means that unless you want to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
