# Fritzing sketch 4x4kb_via_mcp23017 (saved by Fritzing 0.9.3b)

parts:
  S1 = Pushbutton [package="[THT]"]
  S2 = Pushbutton [package="[THT]"]
  S3 = Pushbutton [package="[THT]"]
  S4 = Pushbutton [package="[THT]"]
  S5 = Pushbutton [package="[THT]"]
  S6 = Pushbutton [package="[THT]"]
  S7 = Pushbutton [package="[THT]"]
  S8 = Pushbutton [package="[THT]"]
  S9 = Pushbutton [package="[THT]"]
  S10 = Pushbutton [package="[THT]"]
  S11 = Pushbutton [package="[THT]"]
  S12 = Pushbutton [package="[THT]"]
  S13 = Pushbutton [package="[THT]"]
  S14 = Pushbutton [package="[THT]"]
  S15 = Pushbutton [package="[THT]"]
  S16 = Pushbutton [package="[THT]"]
  R1 = Resistor [tolerance=±5% resistance=22k package=THT]
  R2 = Resistor [tolerance=±5% resistance=22k package=THT]
  R3 = Resistor [tolerance=±5% resistance=22k package=THT]
  R4 = Resistor [tolerance=±5% resistance=22k package=THT]
  Raspberry_Pi_1 = Raspberry Pi 3 [part_number=RPI-3-V1.2]
  U1 = mystery part, 28 pins [chip_label=MCP23017]

nets:
  N1: S1.Pin_1, S1.Pin_2, S2.Pin_1, S2.Pin_2, S3.Pin_1, S3.Pin_2, S4.Pin_1, S4.Pin_2, R4.Pin_1, U1.pin25
  N2: S1.Pin_3, S7.Pin_3, S10.Pin_3, S16.Pin_3, U1.pin1
  N3: S2.Pin_3, S8.Pin_3, S12.Pin_3, S14.Pin_3, U1.pin2
  N4: S3.Pin_3, S6.Pin_3, S9.Pin_3, S13.Pin_3, U1.pin3
  N5: S4.Pin_3, S5.Pin_3, S11.Pin_3, S15.Pin_3, U1.pin4
  N6: S5.Pin_1, S5.Pin_2, S6.Pin_1, S6.Pin_2, S7.Pin_1, S7.Pin_2, S8.Pin_1, S8.Pin_2, R3.Pin_1, U1.pin26
  N7: S9.Pin_1, S9.Pin_2, S10.Pin_1, S10.Pin_2, S11.Pin_1, S11.Pin_2, S12.Pin_1, S12.Pin_2, R2.Pin_1, U1.pin27
  N8: S13.Pin_1, S13.Pin_2, S14.Pin_1, S14.Pin_2, S15.Pin_1, S15.Pin_2, S16.Pin_1, S16.Pin_2, R1.Pin_1, U1.pin28
  N9: R1.Pin_0, R2.Pin_0, R3.Pin_0, R4.Pin_0, Raspberry_Pi_1.GND, U1.pin10, U1.pin15, U1.pin16, U1.pin17
  N10: Raspberry_Pi_1.GPIO2, U1.pin13
  N11: Raspberry_Pi_1.GPIO3, U1.pin12
  N12: Raspberry_Pi_1.5V, U1.pin9, U1.pin18
