# Fritzing sketch MAX31856_circuit (saved by Fritzing 0.9.5d)

parts:
  Part1 = Adafruit MAX31865 RTD Sensor Breakout [part_number="Adafruit #3328"]
  Raspberry_Pi_1 = Raspberry Pi 3 [part_number=RPI-3-V1.2]

nets:
  VIN: Part1.VIN, Raspberry_Pi_1.3V3
  GND: Part1.GND, Raspberry_Pi_1.GND
  N1: Part1.SCLK, Raspberry_Pi_1.GIPO11
  N2: Part1.SDO, Raspberry_Pi_1.GIPO9
  N3: Part1.SDI, Raspberry_Pi_1.GIPO10
  N4: Part1.CS, Raspberry_Pi_1.GIPO8

custom parts:
  Adafruit MAX31865 RTD Sensor Breakout: For precision temperature sensing, nothing beats a Platinum RTD. Resistance temperature detectors (RTDs) are temperature sensors that contain a resistor that changes resistance value as its temperature changes, basically a kind of thermistor. In this sensor, the resistor is actually a small strip of Platinum with a resistance of 100 ohms at 0°C, thus the name PT100. Compared to most NTC/PTC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
