# Fritzing sketch Mcp23S17_Spi_ReadSwitches_WriteLeds (saved by Fritzing 0.9.3b)
perfboards: 1

parts:
  R6 = Resistor [tolerance=±5% resistance=10k package=THT]
  R8 = Resistor [tolerance=±5% resistance=10k package=THT]
  R24 = Resistor [tolerance=±5% resistance=220 package=THT]
  R13 = Resistor [tolerance=±5% resistance=10k package=THT]
  R5 = Resistor [tolerance=±5% resistance=10k package=THT]
  R23 = Resistor [tolerance=±5% resistance=220 package=THT]
  LED14 = LED - 3mm [color="Red (633nm)" package="3 mm [THT]"]
  R22 = Resistor [tolerance=±5% resistance=220 package=THT]
  LED10 = LED - 3mm [color="Red (633nm)" package="3 mm [THT]"]
  LED15 = LED - 3mm [color="Red (633nm)" package="3 mm [THT]"]
  LED16 = LED - 3mm [color="Red (633nm)" package="3 mm [THT]"]
  LED17 = LED - 3mm [color="Red (633nm)" package="3 mm [THT]"]
  R2 = Resistor [tolerance=±5% resistance=10k package=THT]
  SW1 = DIP Switch 8 Position [package=dipswitch-08]
  LED12 = LED - 3mm [color="Red (633nm)" package="3 mm [THT]"]
  R7 = Resistor [tolerance=±5% resistance=10k package=THT]
  R4 = Resistor [tolerance=±5% resistance=10k package=THT]
  R10 = Resistor [tolerance=±5% resistance=10k package=THT]
  R25 = Resistor [tolerance=±5% resistance=220 package=THT]
  R3 = Resistor [tolerance=±10% resistance=10k package=THT]
  R20 = Resistor [tolerance=±5% resistance=220 package=THT]
  LED9 = LED - 3mm [color="Red (633nm)" package="3 mm [THT]"]
  LED11 = LED - 3mm [color="Red (633nm)" package="3 mm [THT]"]
  R26 = Resistor [tolerance=±5% resistance=220 package=THT]
  R19 = Resistor [tolerance=±5% resistance=220 package=THT]
  R21 = Resistor [tolerance=±5% resistance=220 package=THT]
  IC1 = MCP23017 I2C I/O Expander [part_number=MCP23S17]
  Raspberry_Pi_1 = Raspberry Pi 3 [part_number=RPI-3-V1.2]

nets:
  VDD: R6.Pin_0, R8.Pin_0, R13.Pin_0, R5.Pin_0, R2.Pin_0, R7.Pin_0, R4.Pin_0, R10.Pin_0, R3.Pin_0, IC1.VDD, Raspberry_Pi_1.5V
  N1: R6.Pin_1, SW1.11, IC1.GPA2
  N2: R8.Pin_1, SW1.9, IC1.GPA0
  N3: R24.Pin_0, IC1.GPB7
  N4: R24.Pin_1, LED9.cathode
  N5: R13.Pin_1, SW1.16, IC1.GPA7
  N6: R5.Pin_1, SW1.12, IC1.GPA3
  N7: R23.Pin_0, IC1.GPB5
  N8: R23.Pin_1, LED11.cathode
  N9: LED14.cathode, R20.Pin_1
  N10: LED14.anode, LED10.anode, LED15.anode, LED16.anode, LED17.anode, LED12.anode, LED9.anode, LED11.anode
  N11: R22.Pin_0, IC1.GPB3
  N12: R22.Pin_1, LED16.cathode
  N13: LED10.cathode, R25.Pin_1
  N14: LED15.cathode, R21.Pin_1
  N15: LED17.cathode, R19.Pin_1
  N16: R2.Pin_1, SW1.15, IC1.GPA6
  GND: SW1.8, IC1.VSS, IC1.A0, IC1.A2, Raspberry_Pi_1.GND
  N17: SW1.10, R7.Pin_1, IC1.GPA1
  N18: SW1.13, R4.Pin_1, IC1.GPA4
  N19: SW1.14, R3.Pin_1, IC1.GPA5
  N20: LED12.cathode, R26.Pin_1
  N21: R10.Pin_1, IC1.RESET
  N22: R25.Pin_0, IC1.GPB6
  N23: R20.Pin_0, IC1.GPB1
  N24: R26.Pin_0, IC1.GPB4
  N25: R19.Pin_0, IC1.GPB0
  N26: R21.Pin_0, IC1.GPB2
  N27: IC1.NC#11, Raspberry_Pi_1.GIPO8
  N28: IC1.SCL, Raspberry_Pi_1.GIPO11
  N29: IC1.SDA, Raspberry_Pi_1.GIPO10
  N30: IC1.NC#14, Raspberry_Pi_1.GIPO9

notes:
  NOTE: This circuit uses MCP23S17 that offers SPI interface.

custom parts:
  MCP23017 I2C I/O Expander: The MCP23017 uses two i2c pins (these can be shared with other i2c devices), and in exchange gives you 16 general purpose pins. You can set each of 16 pins to be input, output, input with a pullup or open drain. There's even the ability to get an interrupt via an external pin when any of the inputs change so you don't have to keep polling the chip.
