# Fritzing sketch LSxxxB7DHxx (saved by Fritzing 0.9.4)

parts:
  U1 = mystery part, 10 pins [chip_label=LSxxxB7DHxx]
  Raspberry_Pi_1 = Raspberry Pi 3 [part_number=RPI-3-V1.2]

nets:
  N1: U1.pin1, Raspberry_Pi_1.GPIO11
  N2: U1.pin2, Raspberry_Pi_1.GPIO10
  N3: U1.pin3, Raspberry_Pi_1.GPIO25
  N4: U1.pin4, Raspberry_Pi_1.GPIO23
  N5: U1.pin5, Raspberry_Pi_1.GPIO24
  N6: U1.pin6, U1.pin7, Raspberry_Pi_1.3v3
  N7: U1.pin8, U1.pin9, U1.pin10, Raspberry_Pi_1.GND
