# Fritzing sketch MLX90614_circuit (saved by Fritzing 0.9.3b)

parts:
  Raspberry_Pi_1 = Raspberry Pi 3 [part_number=RPI-3-V1.2]
  U2 = MLX90614 [package=to-39]

nets:
  N1: Raspberry_Pi_1.GPIO2, U2.PWM_SDA
  N2: Raspberry_Pi_1.GPIO3, U2.SCL_VZ
  5V: Raspberry_Pi_1.5V, U2.VDD, U2.VSS
