# Fritzing sketch Mpu6050 (saved by Fritzing 0.9.5d)

parts:
  Raspberry_Pi_1 = Raspberry Pi 3 [part_number=RPI-3-V1.2]
  Компонент1 = InvenSense MPU6050

nets:
  N1: Raspberry_Pi_1.GPIO2, Компонент1.SDA
  N2: Raspberry_Pi_1.GPIO3, Компонент1.SCL
  GND: Raspberry_Pi_1.GND, Компонент1.GND
  5V: Raspberry_Pi_1.5V, Компонент1.VCC

notes:
  Also 3.3V supported
