# Fritzing sketch Mpu9250 (saved by Fritzing 0.9.3b)

parts:
  Raspberry_Pi_1 = Raspberry Pi 3 [part_number=RPI-3-V1.2]
  MPU9250_MPU-1 = SparkFun IMU Breakout - MPU-9250 [part_number=" SEN-13762"]

nets:
  3V3: Raspberry_Pi_1.3v3, Raspberry_Pi_1.3V3, MPU9250_MPU-1.VDD, MPU9250_MPU-1.VDDIO
  N1: Raspberry_Pi_1.GPIO2, MPU9250_MPU-1.SDA/SDI
  N2: Raspberry_Pi_1.GPIO3, MPU9250_MPU-1.SCL/SCLK
  GND: Raspberry_Pi_1.GND, MPU9250_MPU-1.GND, MPU9250_MPU-1.FSYNC, MPU9250_MPU-1.AD0/SDO
