# Fritzing sketch SerialPortInterfaces (saved by Fritzing 0.9.6b)
breadboards: 1

parts:
  Part8 = Joy-It bi-directional level shifter [part_number="Level Shifter1"]
  R43 = Resistor [tolerance=±5% resistance=4700 power=0.25 package=THT]
  X1 = DB9 Connector [package=db9]
  IC5 = IC, DIP package, 14 pins [chip_label=SN74HC part_number="Uart Transformer"]
  R45 = Resistor [tolerance=±5% resistance=2200 power=0.25 package=THT]
  R46 = Resistor [tolerance=±5% resistance=1500 power=0.25 package=THT]
  R47 = Resistor [tolerance=±5% resistance=4700 power=0.25 package=THT]
  X2 = DB9 Connector [package=db9]
  Raspberry_Pi_1 = Raspberry Pi 4B

nets:
  N1: Part8.A4, Raspberry_Pi_1.GPIO4
  N2: Part8.A3, Raspberry_Pi_1.GPIO5
  N3: Part8.VCCa, Raspberry_Pi_1.3V3
  N4: Part8.VCCb, IC5.pin14, Raspberry_Pi_1.5V
  N5: Part8.B3, IC5.pin3
  N6: Part8.B4, IC5.pin12, IC5.pin13
  N7: R43.Pin_0, X1.2
  N8: R43.Pin_1, IC5.pin1, IC5.pin2
  N9: X1.3, IC5.pin11
  N10: X1.7, IC5.pin7, R45.Pin_1, X2.7, Raspberry_Pi_1.GND
  N11: IC5.pin4, IC5.pin5, R47.Pin_1
  N12: IC5.pin6, R46.Pin_0
  N13: IC5.pin8, X2.3
  N14: IC5.pin9, IC5.pin10, Raspberry_Pi_1.ID_SC
  N15: R45.Pin_0, R46.Pin_1, Raspberry_Pi_1.ID_SD
  N16: R47.Pin_0, X2.2

custom parts:
  Joy-It bi-directional level shifter: This is an interface board to connect 5V chips to 3.3V CPUs. I2C capable.
