# Fritzing sketch NRF_circuit (saved by Fritzing 0.9.3b)

parts:
  元件1 = NRF24L01
  元件2 = NRF24L01
  Raspberry_Pi_1 = Raspberry Pi 3 [part_number=RPI-3-V1.2]

nets:
  N1: 元件1.IRQ, Raspberry_Pi_1.GPIO24
  N2: 元件1.MOSI, Raspberry_Pi_1.GPIO10
  N3: 元件1.CSN, Raspberry_Pi_1.GPIO8
  VCC: 元件1.VCC, 元件2.VCC, Raspberry_Pi_1.5V
  N4: 元件1.MISO, Raspberry_Pi_1.GPIO9
  N5: 元件1.SCK, Raspberry_Pi_1.GPIO11
  N6: 元件1.CE, Raspberry_Pi_1.GPIO23
  GND: 元件1.GND, 元件2.GND, Raspberry_Pi_1.GND
  N7: 元件2.IRQ, Raspberry_Pi_1.GPIO19
  N8: 元件2.MOSI, Raspberry_Pi_1.GPIO20
  N9: 元件2.CSN, Raspberry_Pi_1.GPIO16
  N10: 元件2.MISO, Raspberry_Pi_1.GPIO6
  N11: 元件2.SCK, Raspberry_Pi_1.GPIO21
  N12: 元件2.CE, Raspberry_Pi_1.GPIO5

notes:
  nRF1
  VCC - 3.3V (Best)
  GND - GND
  MOSI - SPI0 MOSI (GPIO 10)
  MISO - SPI0 MISO (GPIO 9)
  SCK - SPI0 SCLK (GPIO 11)
  CSN - SPI0 CS0 (GPIO 8)
  CE - GPIO 23
  IRQ - GPIO 24
  nRF2
  VCC - 3.3V (Best)
  GND - GND
  MOSI - SPI1 MOSI (GPIO 20)
  MISO - SPI1 MISO (GPIO 19)
  SCK - SPI1 SCLK (GPIO 21)
  CSN - SPI1 CS0 (GPIO 16)
  CE - GPIO 5
  IRQ - GPIO 6
