# Fritzing sketch onewire-temp (saved by Fritzing 0.9.3b)
breadboards: 1

parts:
  Raspberry_Pi_1 = Raspberry Pi 3 [part_number=RPI-3-V1.2]
  DS1 = DS18B20 1-Wire Temperature Sensor [part_number=DS18B20]
  R1 = Resistor [tolerance=±5% resistance=4.7k package=THT]

nets:
  N1: Raspberry_Pi_1.GPIO4, R1.Pin_0
  GND: Raspberry_Pi_1.GND, DS1.GND
  5V: Raspberry_Pi_1.5V, DS1.VDD
  N2: DS1.DQ, R1.Pin_1
