# Fritzing sketch Pca95x4_I2c_WriteLeds (saved by Fritzing 0.9.3b)
breadboards: 1

parts:
  R1 = Resistor [tolerance=±5% resistance=470 package=THT]
  LED1 = LED - 5mm [color="Red (633nm)" package="5 mm [THT]"]
  R2 = Resistor [tolerance=±5% resistance=10k package=THT]
  R3 = Resistor [tolerance=±5% resistance=470 package=THT]
  LED2 = LED - 5mm [color="Red (633nm)" package="5 mm [THT]"]
  R4 = Resistor [tolerance=±5% resistance=470 package=THT]
  LED3 = LED - 5mm [color="Red (633nm)" package="5 mm [THT]"]
  R5 = Resistor [tolerance=±5% resistance=470 package=THT]
  LED4 = LED - 5mm [color="Red (633nm)" package="5 mm [THT]"]
  R6 = Resistor [tolerance=±5% resistance=470 package=THT]
  LED5 = LED - 5mm [color="Red (633nm)" package="5 mm [THT]"]
  LED6 = LED - 5mm [color="Red (633nm)" package="5 mm [THT]"]
  LED7 = LED - 5mm [color="Red (633nm)" package="5 mm [THT]"]
  LED8 = LED - 5mm [color="Red (633nm)" package="5 mm [THT]"]
  R7 = Resistor [tolerance=±5% resistance=470 package=THT]
  R8 = Resistor [tolerance=±5% resistance=470 package=THT]
  R9 = Resistor [tolerance=±5% resistance=470 package=THT]
  Raspberry_Pi_1 = Raspberry Pi 3 [part_number=RPI-3-V1.2]
  IOE1 = Pca95x4 [package=dil16]

nets:
  N1: R1.Pin_0, LED1.cathode
  N2: R1.Pin_1, IOE1.P0
  3V3: LED1.anode, R2.Pin_0, LED2.anode, LED3.anode, LED4.anode, LED5.anode, LED6.anode, LED7.anode, LED8.anode, Raspberry_Pi_1.3v3, IOE1.Vcc
  N3: R2.Pin_1, IOE1.INT'
  N4: R3.Pin_0, LED2.cathode
  N5: R3.Pin_1, IOE1.P1
  N6: R4.Pin_0, LED3.cathode
  N7: R4.Pin_1, IOE1.P2
  N8: R5.Pin_0, LED4.cathode
  N9: R5.Pin_1, IOE1.P3
  N10: R6.Pin_0, LED5.cathode
  N11: R6.Pin_1, IOE1.P4
  N12: LED6.cathode, R8.Pin_0
  N13: LED7.cathode, R9.Pin_0
  N14: LED8.cathode, R7.Pin_0
  N15: R7.Pin_1, IOE1.P5
  N16: R8.Pin_1, IOE1.P6
  N17: R9.Pin_1, IOE1.P7
  N18: Raspberry_Pi_1.GPIO2, IOE1.SDA
  N19: Raspberry_Pi_1.GPIO3, IOE1.SCL
  N20: Raspberry_Pi_1.GIPO14, IOE1.A0, IOE1.A1, IOE1.A2, IOE1.Ground

custom parts:
  Pca95x4: The PCA95x4 provides 8 bits of General Purpose parallel Input/Output (GPIO) expansion for I2C-bus applications.
