# Fritzing sketch RotaryEncoder.Sample (saved by Fritzing 0.9.3b)
breadboards: 1

parts:
  Part1 = Adafruit T-Cobbler Plus [part_number="Adafruit #1989 and #2028"]
  RE1 = Switched Rotary Encoder [package=THT]

nets:
  N1: Part1.GND, RE1.EncoderPinC
  N2: Part1.GPIO5, RE1.EncoderPinB
  N3: Part1.GPIO6, RE1.EncoderPinA

custom parts:
  Adafruit T-Cobbler Plus: The Raspberry Pi has landed on the Maker World like a 40-GPIO pinned, quad-USB ported, credit card sized bomb of DIY joy. And while you can use most of our great Model B accessories by hooking up our downgrade cable, its probably a good time to upgrade your set up and accessorize using all of the 40 pins. That's why we now carry the Assembled Adafruit Pi T-Cobbler Plus - Breakout + Cable for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
  Switched Rotary Encoder: Rotary Encoder from ALPS STEC12E07.
