# Fritzing sketch SeesawSampleEncoder (saved by Fritzing 0.9.10b)

parts:
  Raspberry_Pi_1 = Raspberry Pi 3 [part_number=RPI-3-V1.2]
  Bauteil1 = Adafruit I2C QT Rotary Encoder [part_number="Adafruit #4991"]

nets:
  N1: Raspberry_Pi_1.GPIO2, Bauteil1.SDA
  N2: Raspberry_Pi_1.GPIO3, Bauteil1.SCL
  3V3: Raspberry_Pi_1.3V3, Bauteil1.VCC
  GND: Raspberry_Pi_1.GND, Bauteil1.GND
  N3: Raspberry_Pi_1.GIPO6, Bauteil1.INT

custom parts:
  Adafruit I2C QT Rotary Encoder: Rotary encoders are soooo much fun! Twist em this way, then twist them that way. Unlike potentiometers, they go all the way around, and often have little detents for tactile feedback. But, if you've ever tried to add encoders to your project you know that they're a real challenge to use: timers, interrupts, debouncing... This Stemma QT breakout makes all that frustration go away - solder in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
