# Fritzing sketch SHT3x_circuit (saved by Fritzing 0.9.3b)

parts:
  Part15 = Adafruit SHT31-D Sensirion Temperature/Humidity Sensor [part_number="Adafruit #2857"]
  Raspberry_Pi_1 = Raspberry Pi 3 [part_number=RPI-3-V1.2]

nets:
  VIN: Part15.VIN, Raspberry_Pi_1.5V
  GND: Part15.GND, Part15.ADDR, Raspberry_Pi_1.GND
  N1: Part15.SCL, Raspberry_Pi_1.GPIO3
  N2: Part15.SDA, Raspberry_Pi_1.GPIO2

custom parts:
  Adafruit SHT31-D Sensirion Temperature/Humidity Sensor: Sensirion Temperature/Humidity sensors are some of the finest & highest-accuracy devices you can get. And, finally we have some that have a true I2C interface for easy reading. The SHT31-D sensor has an excellent ±2% relative humidity and ±0.3°C accuracy for most uses. Unlike earlier SHT sensors, this sensor has a true I2C interface, and (bonus!) even with two address options. It also is 3V or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
