# Fritzing sketch sn74hc595-led-bar-graph (saved by Fritzing 0.9.4)
breadboards: 1

parts:
  Raspberry_Pi_1 = Raspberry Pi 3 [part_number=RPI-3-V1.2]
  U1 = 74HC595 [package="DIP16 [THT]"]
  D1 = LED_BARGRAPH_10 [package=led_bargaph_10]
  R1 = Resistor [tolerance=±5% resistance=220 package="1206 [SMD]"]
  R2 = Resistor [tolerance=±5% resistance=220 package="1206 [SMD]"]
  R4 = Resistor [tolerance=±5% resistance=220 package="1206 [SMD]"]
  R7 = Resistor [tolerance=±5% resistance=220 package="1206 [SMD]"]
  R9 = Resistor [tolerance=±5% resistance=220 package="1206 [SMD]"]
  R10 = Resistor [tolerance=±5% resistance=220 package="1206 [SMD]"]
  R11 = Resistor [tolerance=±5% resistance=220 package="1206 [SMD]"]
  R12 = Resistor [tolerance=±5% resistance=220 package="1206 [SMD]"]

nets:
  N1: Raspberry_Pi_1.GPIO10, U1.MR
  N2: Raspberry_Pi_1.GPIO11, U1.SH_CP
  N3: Raspberry_Pi_1.GPIO13, U1.OE
  N4: Raspberry_Pi_1.GPIO12, U1.ST_CP
  N5: Raspberry_Pi_1.GPIO14, U1.DS
  GND: Raspberry_Pi_1.GND, U1.GND, R1.Pin_0, R2.Pin_0, R4.Pin_0, R7.Pin_0, R9.Pin_0, R10.Pin_0, R11.Pin_0, R12.Pin_0
  5V: Raspberry_Pi_1.5V, U1.VCC
  N6: U1.Q1, D1.B_A
  N7: U1.Q2, D1.C_A
  N8: U1.Q3, D1.D_A
  N9: U1.Q4, D1.E_A
  N10: U1.Q5, D1.F_A
  N11: U1.Q6, D1.G_A
  N12: U1.Q7, D1.H_A
  N13: U1.Q0, D1.A_A
  N14: D1.J_C, D1.C_C, R12.Pin_1
  N15: D1.H_C, R10.Pin_1
  N16: D1.G_C, R11.Pin_1
  N17: D1.F_C, R9.Pin_1
  N18: D1.E_C, R7.Pin_1
  N19: D1.D_C, R1.Pin_1
  N20: D1.B_C, R4.Pin_1
  N21: D1.A_C, R2.Pin_1
