# Fritzing sketch Ssd1351.Sample (saved by Fritzing 0.9.3b)

parts:
  Part1 = OLED Color 1.5 inch 128x128 w microSD [part_number=1431]
  Raspberry_Pi_1 = Raspberry Pi 3 [part_number=RPI-3-V1.2]

nets:
  N1: Part1.MOSI, Raspberry_Pi_1.GPIO10
  N2: Part1.SCK, Raspberry_Pi_1.GPIO11
  N3: Part1.DC, Raspberry_Pi_1.GPIO23
  N4: Part1.RESET, Raspberry_Pi_1.GPIO24
  N5: Part1.OLED_CS, Raspberry_Pi_1.GPIO8
  VIN: Part1.VIN, Raspberry_Pi_1.5V
  GND: Part1.GND, Raspberry_Pi_1.GND

custom parts:
  OLED Color 1.5 inch 128x128 w microSD: The visible portion of this OLED measures 1.5" diagonal and contains 128x128 RGB pixels, each one made of red, green and blue OLEDs. Each pixel can be set with 16-bits of resolution for a large range of colors. Because the display uses OLEDs, there is no backlight, and the contrast is very high (black is really black). We picked this display for its excellent color, this is the nicest mini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
