# Fritzing sketch TCA9548A_usage (saved by Fritzing 0.9.10b)
breadboards: 1

parts:
  Mod1 = Raspberry Pi 4B
  Part1 = Barometric Pressure Sensor - BMP180 Breakout (GY-68)
  Part2 = Barometric Pressure Sensor - BMP180 Breakout (GY-68)
  Part3 = Barometric Pressure Sensor - BMP180 Breakout (GY-68)
  Part4 = Barometric Pressure Sensor - BMP180 Breakout (GY-68)
  Part5 = Adafruit BNO085 9-DOF Orientation IMU Fusion [part_number="Addfruit #4754"]
  Part6 = Adafruit TCA9548A
  Part7 = Adafruit BNO085 9-DOF Orientation IMU Fusion [part_number="Addfruit #4754"]

nets:
  VCC: Mod1.3V3, Part1.VCC, Part2.VCC, Part3.VCC, Part4.VCC, Part5.3.3V, Part6.VCC, Part7.3.3V
  N1: Mod1.GPIO2, Part6.INPUTSDA
  N2: Mod1.GPIO3, Part6.INPUTSCL
  GND: Mod1.GND, Part1.GND, Part2.GND, Part3.GND, Part4.GND, Part5.GND, Part6.GND, Part6.A0, Part6.A1, Part6.A2, Part7.GND
  N3: Part1.SCL, Part6.5SCL
  N4: Part1.SDA, Part6.5SDA
  N5: Part2.SCL, Part6.2SCL
  N6: Part2.SDA, Part6.2SDA
  N7: Part3.SCL, Part6.3SCL
  N8: Part3.SDA, Part6.3SDA
  N9: Part4.SCL, Part6.4SCL
  N10: Part4.SDA, Part6.4SDA
  N11: Part5.SCL/SCK/RX, Part6.0SCL
  N12: Part5.SDA/MISO/TX, Part6.0SDA
  N13: Part6.1SDA, Part7.SDA/MISO/TX
  N14: Part6.1SCL, Part7.SCL/SCK/RX

custom parts:
  Adafruit TCA9548A: You just found the perfect I2C sensor, and you want to wire up two or three or more of them to your Arduino when you realize "Uh oh, this chip has a fixed I2C address, and from what I know about I2C, you cannot have two devices with the same address on the same SDA/SCL pins!" Are you out of luck? You would be, if you didn't have this ultra-cool TCA9548A 1-to-8 I2C multiplexer! Finally, a way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
