# Fritzing sketch tm1637 (saved by Fritzing 0.9.3b)

parts:
  Grove2 = Grove 4 Digit Display
  Raspberry_Pi_1 = Raspberry Pi 3 [part_number=RPI-3-V1.2]

nets:
  GND: Grove2.GND, Raspberry_Pi_1.GND
  VCC: Grove2.VCC, Raspberry_Pi_1.5V
  N1: Grove2.DIO, Raspberry_Pi_1.GPIO21
  N2: Grove2.CLK, Raspberry_Pi_1.GPIO20
