# Fritzing sketch Uln2003 (saved by Fritzing 0.9.3b)

parts:
  MOTOR1 = 28BYJ-48 Stepper Motor
  X1 = X113647
  Raspberry_Pi1 = Raspberry Pi B+
  VCC1 = Battery block 9V

nets:
  N1: MOTOR1.BLUE, X1.connector7
  N2: MOTOR1.PINK, X1.connector8
  N3: MOTOR1.RED, X1.connector11
  N4: MOTOR1.ORANGE, X1.connector10
  N5: MOTOR1.YELLOW, X1.connector9
  N6: X1.connector1, Raspberry_Pi1.GPIO4
  N7: X1.connector2, Raspberry_Pi1.GPIO17
  N8: X1.connector3, Raspberry_Pi1.GPIO27
  N9: X1.connector4, Raspberry_Pi1.GPIO22
  N10: X1.connector5, Raspberry_Pi1.GND, VCC1.-
  N11: X1.connector6, VCC1.+

custom parts:
  28BYJ-48 Stepper Motor: 28BYJ-48 gear-reduction stepper motor (small)
