# Fritzing sketch test_setup (saved by Fritzing 1.0.1rc)
breadboards: 1

parts:
  Mod1 = Raspberry Pi 4B
  LED = LED - 3mm [color="Red (633nm)" current=0.030A package="3 mm [THT]"]
  Q2 = NPN-Transistor [package="TO92 [THT]"]
  Adafruit_VCNL1 = Adafruit VCNL4040
  C2 = Electrolytic Capacitor [capacitance=1000µF voltage=16V package="300 mil [THT, electrolytic]"]
  R2 = Resistor [tolerance=±5% power=0.25W resistance=100 package=THT]
  R1 = Resistor [tolerance=±5% resistance=10k package="0402 [SMD]"]

nets:
  5V: Mod1.5V, Adafruit_VCNL1.VCC, C2.+, R2.Pin_1, R1.Pin_1
  N1: Mod1.GPIO2, Adafruit_VCNL1.SDA
  N2: Mod1.GPIO3, Adafruit_VCNL1.SCL
  GND: Mod1.GND, Q2.E, Adafruit_VCNL1.GND, C2.-
  N3: LED.cathode, Q2.C
  N4: LED.anode, R2.Pin_0
  N5: Q2.B, Adafruit_VCNL1.INT, R1.Pin_0

notes:
  BC547B
