# Fritzing sketch rpi-neo-pixels (saved by Fritzing 0.9.3b)

parts:
  U1 = WS2812 RGB LED matrix 1x8
  Raspberry_Pi_1 = Raspberry Pi 3 [part_number=RPI-3-V1.2]

nets:
  GND: U1.GND, Raspberry_Pi_1.GND
  VCC: U1.VCC, Raspberry_Pi_1.5V
  N1: U1.DIN, Raspberry_Pi_1.GPIO10

custom parts:
  WS2812 RGB LED matrix 1x8: WS2812 matrix 1x8
